// Logisim project S1-T16.circ as structural Verilog: 7 circuits, main circuit main
module main (
  input  RESET_CIRCUIT,
  input  SET_BOMB,
  input  [3:0] BOX_LOCATION_INT_THE_GRID,
  input  CONFIRM_THE_BOX,
  output [3:0] NUMBER_OF_BOMBS,
  output [3:0] NUMBER_OF_BOXES_OPENED,
  output GAME_WON,
  output GAME_OVER,
  output _0000,
  output _0100,
  output _1000,
  output _1100,
  output _0001,
  output _0101,
  output _1001,
  output _1101,
  output _0010,
  output _0110,
  output _1010,
  output _1110,
  output _0011,
  output _0111,
  output _1011,
  output _1111
);

  outputs outputs_1 (
    .RNG_CLICK(SET_BOMB), .in_2(RESET_CIRCUIT), .OUTPUT_COUNTER(NUMBER_OF_BOMBS), .out_6(_0000),
    .out_7(_0100), .out_8(_1000), .out_9(_1100), .GAME_WON(GAME_WON), .out_11(_0001), .out_12(_0101),
    .out_13(_1001), .out_14(_1101), .GAME_OVER(GAME_OVER), .out_16(_0010), .out_17(_0110), .out_18(_1010),
    .out_19(_1110), .out_20(_0011), .out_21(_0111), .out_22(_1011), .out_23(_1111),
    .INPUT_COUNTER(NUMBER_OF_BOXES_OPENED), .in_4(CONFIRM_THE_BOX), .INPUT(BOX_LOCATION_INT_THE_GRID));

  // Notes on the sheet:
  //   THE GAME OF MINES
  //   OUTPUTS
endmodule

module grids (
  input  ENABLE,
  input  RESET,
  output out_3,
  output out_4,
  output out_5,
  output out_6,
  output out_7,
  output out_8,
  output out_9,
  output out_10,
  output [3:0] COUNTER,
  output out_12,
  output out_13,
  output out_14,
  output out_15,
  output out_16,
  output out_17,
  output out_18,
  output out_19
);

  wire decoder_1_out0, decoder_1_out1, decoder_1_out2, decoder_1_out3, decoder_1_out4, decoder_1_out5,
       decoder_1_out6, decoder_1_out7, decoder_1_out8, decoder_1_out9, decoder_1_out10, decoder_1_out11,
       decoder_1_out12, decoder_1_out13, decoder_1_out14, decoder_1_out15, xor_1_out;
  wire [3:0] RANDOM_NUMBER_GENERATOR_out_2;

  Decoder #(.select(4)) decoder_1 (
    .out0(decoder_1_out0), .out1(decoder_1_out1), .out2(decoder_1_out2), .out3(decoder_1_out3),
    .out4(decoder_1_out4), .out5(decoder_1_out5), .out6(decoder_1_out6), .out7(decoder_1_out7),
    .out8(decoder_1_out8), .out9(decoder_1_out9), .out10(decoder_1_out10), .out11(decoder_1_out11),
    .out12(decoder_1_out12), .out13(decoder_1_out13), .out14(decoder_1_out14), .out15(decoder_1_out15),
    .sel(RANDOM_NUMBER_GENERATOR_out_2));  // open: en
  D_Flip_Flop d_ff_1 (.clk(ENABLE), .D(1'b1), .Q(out_3), .en(decoder_1_out3), .reset(RESET));  // open: Qn, preset
  D_Flip_Flop d_ff_2 (.clk(ENABLE), .D(1'b1), .Q(out_7), .en(decoder_1_out2), .reset(RESET));  // open: Qn, preset
  D_Flip_Flop d_ff_3 (.clk(ENABLE), .D(1'b1), .Q(out_12), .en(decoder_1_out1), .reset(RESET));  // open: Qn, preset
  D_Flip_Flop d_ff_4 (.clk(ENABLE), .D(1'b1), .Q(out_16), .en(decoder_1_out0), .reset(RESET));  // open: Qn, preset
  D_Flip_Flop d_ff_5 (.clk(ENABLE), .D(1'b1), .Q(out_4), .en(decoder_1_out7), .reset(RESET));  // open: Qn, preset
  D_Flip_Flop d_ff_6 (.clk(ENABLE), .D(1'b1), .Q(out_8), .en(decoder_1_out6), .reset(RESET));  // open: Qn, preset
  D_Flip_Flop d_ff_7 (.clk(ENABLE), .D(1'b1), .Q(out_14), .en(decoder_1_out5), .reset(RESET));  // open: Qn, preset
  D_Flip_Flop d_ff_8 (.clk(ENABLE), .D(1'b1), .Q(out_17), .en(decoder_1_out4), .reset(RESET));  // open: Qn, preset
  rng RANDOM_NUMBER_GENERATOR (
    .RESET(RESET), .out_5(RANDOM_NUMBER_GENERATOR_out_2[3]), .out_3(RANDOM_NUMBER_GENERATOR_out_2[2]),
    .out_4(RANDOM_NUMBER_GENERATOR_out_2[1]), .out_2(RANDOM_NUMBER_GENERATOR_out_2[0]));
  D_Flip_Flop d_ff_9 (.clk(ENABLE), .D(1'b1), .Q(out_5), .en(decoder_1_out11), .reset(RESET));  // open: Qn, preset
  D_Flip_Flop d_ff_10 (.clk(ENABLE), .D(1'b1), .Q(out_9), .en(decoder_1_out10), .reset(RESET));  // open: Qn, preset
  D_Flip_Flop d_ff_11 (.clk(ENABLE), .D(1'b1), .Q(out_15), .en(decoder_1_out9), .reset(RESET));  // open: Qn, preset
  D_Flip_Flop d_ff_12 (.clk(ENABLE), .D(1'b1), .Q(out_18), .en(decoder_1_out8), .reset(RESET));  // open: Qn, preset
  D_Flip_Flop d_ff_13 (.clk(ENABLE), .D(1'b1), .Q(out_6), .en(decoder_1_out15), .reset(RESET));  // open: Qn, preset
  D_Flip_Flop d_ff_14 (.clk(ENABLE), .D(1'b1), .Q(out_10), .en(decoder_1_out14), .reset(RESET));  // open: Qn, preset
  D_Flip_Flop d_ff_15 (.clk(ENABLE), .D(1'b1), .Q(out_13), .en(decoder_1_out13), .reset(RESET));  // open: Qn, preset
  D_Flip_Flop d_ff_16 (.clk(ENABLE), .D(1'b1), .Q(out_19), .en(decoder_1_out12), .reset(RESET));  // open: Qn, preset
  xor xor_1 (xor_1_out, out_6, out_5, out_4, out_3, out_10, out_9, out_8, out_7, out_12, out_14, out_15, out_13, out_16, out_17, out_18, out_19);
  counter counter_1 (.CHANGE_IN_INPUT(xor_1_out), .RESET(RESET), .ENABLE(ENABLE), .out_4(COUNTER));
endmodule

module rng (
  input  RESET,
  output out_2,
  output out_3,
  output out_4,
  output out_5
);

  wire CLOCK_out, xor_1_out;

  Clock CLOCK (.out(CLOCK_out));
  D_Flip_Flop d_ff_1 (.clk(CLOCK_out), .D(xor_1_out), .Q(out_5), .preset(RESET));  // open: Qn, en, reset
  xor xor_1 (xor_1_out, out_2, out_4);
  D_Flip_Flop d_ff_2 (.clk(CLOCK_out), .D(out_5), .Q(out_3), .reset(RESET));  // open: Qn, preset, en
  D_Flip_Flop d_ff_3 (.clk(CLOCK_out), .D(out_3), .Q(out_4), .reset(RESET));  // open: Qn, preset, en
  D_Flip_Flop d_ff_4 (.clk(CLOCK_out), .D(out_4), .Q(out_2), .reset(RESET));  // open: Qn, preset, en
endmodule

module counter (
  input  CHANGE_IN_INPUT,
  input  RESET,
  input  ENABLE,
  output [3:0] out_4
);

  wire d_ff_1_q, j_k_ff_1_q, j_k_ff_2_q, j_k_ff_3_q, xor_1_out;

  J_K_Flip_Flop j_k_ff_1 (
    .J(1'b1), .clk(ENABLE), .K(1'b1), .Q(j_k_ff_1_q), .Qn(out_4[0]), .preset(RESET), .en(xor_1_out));  // open: reset
  J_K_Flip_Flop j_k_ff_2 (
    .J(1'b1), .clk(j_k_ff_1_q), .K(1'b1), .Q(j_k_ff_2_q), .Qn(out_4[1]), .preset(RESET));  // open: en, reset
  J_K_Flip_Flop j_k_ff_3 (
    .J(1'b1), .clk(j_k_ff_2_q), .K(1'b1), .Q(j_k_ff_3_q), .Qn(out_4[2]), .preset(RESET));  // open: en, reset
  J_K_Flip_Flop j_k_ff_4 (.J(1'b1), .clk(j_k_ff_3_q), .K(1'b1), .Qn(out_4[3]), .preset(RESET));  // open: Q, en, reset
  D_Flip_Flop d_ff_1 (.clk(ENABLE), .D(CHANGE_IN_INPUT), .Q(d_ff_1_q), .preset(RESET));  // open: Qn, en, reset
  xor xor_1 (xor_1_out, d_ff_1_q, CHANGE_IN_INPUT);
endmodule

module outputs (
  input  RNG_CLICK,
  input  in_2,
  input  [3:0] INPUT,
  input  in_4,
  output [3:0] OUTPUT_COUNTER,
  output out_6,
  output out_7,
  output out_8,
  output out_9,
  output GAME_WON,
  output out_11,
  output out_12,
  output out_13,
  output out_14,
  output GAME_OVER,
  output out_16,
  output out_17,
  output out_18,
  output out_19,
  output out_20,
  output out_21,
  output out_22,
  output out_23,
  output [3:0] INPUT_COUNTER
);

  wire comparator_1_eq, d_flip_flop_1_bomb_detected, d_flip_flop_2_bomb_detected,
       d_flip_flop_3_bomb_detected, d_flip_flop_4_bomb_detected, d_flip_flop_5_bomb_detected,
       d_flip_flop_6_bomb_detected, d_flip_flop_7_bomb_detected, d_flip_flop_8_bomb_detected,
       d_flip_flop_9_bomb_detected, d_flip_flop_10_bomb_detected, d_flip_flop_11_bomb_detected,
       d_flip_flop_12_bomb_detected, d_flip_flop_13_bomb_detected, d_flip_flop_14_bomb_detected,
       d_flip_flop_15_bomb_detected, d_flip_flop_16_bomb_detected, decoder_1_out0, decoder_1_out1,
       decoder_1_out2, decoder_1_out3, decoder_1_out4, decoder_1_out5, decoder_1_out6, decoder_1_out7,
       decoder_1_out8, decoder_1_out9, decoder_1_out10, decoder_1_out11, decoder_1_out12, decoder_1_out13,
       decoder_1_out14, decoder_1_out15, GRIDS_out_3, GRIDS_out_4, GRIDS_out_5, GRIDS_out_6, GRIDS_out_7,
       GRIDS_out_8, GRIDS_out_9, GRIDS_out_10, GRIDS_out_12, GRIDS_out_13, GRIDS_out_14, GRIDS_out_15,
       GRIDS_out_16, GRIDS_out_17, GRIDS_out_18, GRIDS_out_19, not_2_out, xor_2_out;
  wire [3:0] adder_1_out, adder_2_out, not_1_out;

  Decoder #(.select(4)) decoder_1 (
    .out0(decoder_1_out0), .out1(decoder_1_out1), .out2(decoder_1_out2), .out3(decoder_1_out3),
    .out4(decoder_1_out4), .out5(decoder_1_out5), .out6(decoder_1_out6), .out7(decoder_1_out7),
    .out8(decoder_1_out8), .out9(decoder_1_out9), .out10(decoder_1_out10), .out11(decoder_1_out11),
    .out12(decoder_1_out12), .out13(decoder_1_out13), .out14(decoder_1_out14), .out15(decoder_1_out15),
    .sel(INPUT));  // open: en
  d_flip_flop d_flip_flop_1 (
    .SWITCH(in_4), .CONSTANT(1'b1), .DECODER_INPUT(decoder_1_out0), .RESET(in_2), .FINAL_LED_OUTPUT(out_6),
    .BOMB_DETECTED(d_flip_flop_1_bomb_detected), .BOMB(GRIDS_out_16), .GAME_OVER(GAME_OVER));
  d_flip_flop d_flip_flop_2 (
    .SWITCH(in_4), .CONSTANT(1'b1), .DECODER_INPUT(decoder_1_out1), .RESET(in_2), .FINAL_LED_OUTPUT(out_11),
    .BOMB_DETECTED(d_flip_flop_2_bomb_detected), .BOMB(GRIDS_out_12), .GAME_OVER(GAME_OVER));
  d_flip_flop d_flip_flop_3 (
    .SWITCH(in_4), .CONSTANT(1'b1), .DECODER_INPUT(decoder_1_out2), .RESET(in_2), .FINAL_LED_OUTPUT(out_16),
    .BOMB_DETECTED(d_flip_flop_3_bomb_detected), .BOMB(GRIDS_out_7), .GAME_OVER(GAME_OVER));
  d_flip_flop d_flip_flop_4 (
    .SWITCH(in_4), .CONSTANT(1'b1), .DECODER_INPUT(decoder_1_out3), .RESET(in_2), .FINAL_LED_OUTPUT(out_20),
    .BOMB_DETECTED(d_flip_flop_4_bomb_detected), .BOMB(GRIDS_out_3), .GAME_OVER(GAME_OVER));
  d_flip_flop d_flip_flop_5 (
    .SWITCH(in_4), .CONSTANT(1'b1), .DECODER_INPUT(decoder_1_out4), .RESET(in_2), .FINAL_LED_OUTPUT(out_7),
    .BOMB_DETECTED(d_flip_flop_5_bomb_detected), .BOMB(GRIDS_out_17), .GAME_OVER(GAME_OVER));
  d_flip_flop d_flip_flop_6 (
    .SWITCH(in_4), .CONSTANT(1'b1), .DECODER_INPUT(decoder_1_out5), .RESET(in_2), .FINAL_LED_OUTPUT(out_12),
    .BOMB_DETECTED(d_flip_flop_6_bomb_detected), .BOMB(GRIDS_out_14), .GAME_OVER(GAME_OVER));
  grids GRIDS (
    .out_3(GRIDS_out_3), .out_4(GRIDS_out_4), .out_5(GRIDS_out_5), .out_6(GRIDS_out_6), .out_7(GRIDS_out_7),
    .out_8(GRIDS_out_8), .out_9(GRIDS_out_9), .out_10(GRIDS_out_10), .COUNTER(OUTPUT_COUNTER),
    .out_12(GRIDS_out_12), .out_13(GRIDS_out_13), .out_14(GRIDS_out_14), .out_15(GRIDS_out_15),
    .out_16(GRIDS_out_16), .out_17(GRIDS_out_17), .out_18(GRIDS_out_18), .out_19(GRIDS_out_19),
    .ENABLE(RNG_CLICK), .RESET(in_2));
  d_flip_flop d_flip_flop_7 (
    .SWITCH(in_4), .CONSTANT(1'b1), .DECODER_INPUT(decoder_1_out6), .RESET(in_2), .FINAL_LED_OUTPUT(out_17),
    .BOMB_DETECTED(d_flip_flop_7_bomb_detected), .BOMB(GRIDS_out_8), .GAME_OVER(GAME_OVER));
  d_flip_flop d_flip_flop_8 (
    .SWITCH(in_4), .CONSTANT(1'b1), .DECODER_INPUT(decoder_1_out7), .RESET(in_2), .FINAL_LED_OUTPUT(out_21),
    .BOMB_DETECTED(d_flip_flop_8_bomb_detected), .BOMB(GRIDS_out_4), .GAME_OVER(GAME_OVER));
  d_flip_flop d_flip_flop_9 (
    .SWITCH(in_4), .CONSTANT(1'b1), .DECODER_INPUT(decoder_1_out8), .RESET(in_2), .FINAL_LED_OUTPUT(out_8),
    .BOMB_DETECTED(d_flip_flop_9_bomb_detected), .BOMB(GRIDS_out_18), .GAME_OVER(GAME_OVER));
  d_flip_flop d_flip_flop_10 (
    .SWITCH(in_4), .CONSTANT(1'b1), .DECODER_INPUT(decoder_1_out9), .RESET(in_2), .FINAL_LED_OUTPUT(out_13),
    .BOMB_DETECTED(d_flip_flop_10_bomb_detected), .BOMB(GRIDS_out_15), .GAME_OVER(GAME_OVER));
  d_flip_flop d_flip_flop_11 (
    .SWITCH(in_4), .CONSTANT(1'b1), .DECODER_INPUT(decoder_1_out10), .RESET(in_2), .FINAL_LED_OUTPUT(out_18),
    .BOMB_DETECTED(d_flip_flop_11_bomb_detected), .BOMB(GRIDS_out_9), .GAME_OVER(GAME_OVER));
  d_flip_flop d_flip_flop_12 (
    .SWITCH(in_4), .CONSTANT(1'b1), .DECODER_INPUT(decoder_1_out11), .RESET(in_2), .FINAL_LED_OUTPUT(out_22),
    .BOMB_DETECTED(d_flip_flop_12_bomb_detected), .BOMB(GRIDS_out_5), .GAME_OVER(GAME_OVER));
  d_flip_flop d_flip_flop_13 (
    .SWITCH(in_4), .CONSTANT(1'b1), .DECODER_INPUT(decoder_1_out12), .RESET(in_2), .FINAL_LED_OUTPUT(out_9),
    .BOMB_DETECTED(d_flip_flop_13_bomb_detected), .BOMB(GRIDS_out_19), .GAME_OVER(GAME_OVER));
  d_flip_flop d_flip_flop_14 (
    .SWITCH(in_4), .CONSTANT(1'b1), .DECODER_INPUT(decoder_1_out13), .RESET(in_2), .FINAL_LED_OUTPUT(out_14),
    .BOMB_DETECTED(d_flip_flop_14_bomb_detected), .BOMB(GRIDS_out_13), .GAME_OVER(GAME_OVER));
  d_flip_flop d_flip_flop_15 (
    .SWITCH(in_4), .CONSTANT(1'b1), .DECODER_INPUT(decoder_1_out14), .RESET(in_2), .FINAL_LED_OUTPUT(out_19),
    .BOMB_DETECTED(d_flip_flop_15_bomb_detected), .BOMB(GRIDS_out_10), .GAME_OVER(GAME_OVER));
  assign not_1_out = ~OUTPUT_COUNTER;  // NOT_Gate not_1, 4 bits wide
  d_flip_flop d_flip_flop_16 (
    .SWITCH(in_4), .CONSTANT(1'b1), .DECODER_INPUT(decoder_1_out15), .RESET(in_2), .FINAL_LED_OUTPUT(out_23),
    .BOMB_DETECTED(d_flip_flop_16_bomb_detected), .BOMB(GRIDS_out_6), .GAME_OVER(GAME_OVER));
  Adder #(.width(4)) adder_1 (.a(4'b1111), .b(not_1_out), .out(adder_1_out), .cin(1'b1));  // open: cout
  xor xor_1 (GAME_OVER, d_flip_flop_13_bomb_detected, d_flip_flop_9_bomb_detected, d_flip_flop_5_bomb_detected, d_flip_flop_1_bomb_detected, d_flip_flop_14_bomb_detected, d_flip_flop_10_bomb_detected, d_flip_flop_6_bomb_detected, d_flip_flop_2_bomb_detected, d_flip_flop_15_bomb_detected, d_flip_flop_11_bomb_detected, d_flip_flop_7_bomb_detected, d_flip_flop_3_bomb_detected, d_flip_flop_16_bomb_detected, d_flip_flop_12_bomb_detected, d_flip_flop_8_bomb_detected, d_flip_flop_4_bomb_detected);
  xor xor_2 (xor_2_out, out_23, out_19, out_14, out_9, out_22, out_18, out_13, out_8, out_21, out_17, out_12, out_7, out_20, out_16, out_11, out_6);
  output_counter output_counter_1 (.in_1(xor_2_out), .in_2(in_2), .in_3(in_4), .out_4(INPUT_COUNTER));
  Adder #(.width(4)) adder_2 (.a(4'b0000), .b(adder_1_out), .out(adder_2_out), .cin(1'b1));  // open: cout
  not not_2 (not_2_out, GAME_OVER);
  Comparator #(.width(4)) comparator_1 (.a(adder_2_out), .b(INPUT_COUNTER), .eq(comparator_1_eq));  // open: gt, lt
  and and_1 (GAME_WON, comparator_1_eq, not_2_out);
endmodule

module d_flip_flop (
  input  BOMB,
  input  SWITCH,
  input  CONSTANT,
  input  DECODER_INPUT,
  input  RESET,
  input  GAME_OVER,
  output FINAL_LED_OUTPUT,
  output BOMB_DETECTED
);

  wire and_2_out, and_3_out, d_ff_1_q, not_1_out;

  D_Flip_Flop d_ff_1 (.clk(SWITCH), .D(CONSTANT), .Q(d_ff_1_q), .en(DECODER_INPUT), .reset(RESET));  // open: Qn, preset
  not not_1 (not_1_out, GAME_OVER);
  and and_1 (BOMB_DETECTED, BOMB, d_ff_1_q);
  and and_2 (and_2_out, GAME_OVER, BOMB);
  and and_3 (and_3_out, d_ff_1_q, not_1_out);
  or or_1 (FINAL_LED_OUTPUT, and_2_out, and_3_out);
endmodule

module output_counter (
  input  in_1,
  input  in_2,
  input  in_3,
  output [3:0] out_4
);

  wire d_ff_1_q, j_k_ff_1_q, j_k_ff_2_q, j_k_ff_3_q, xor_1_out;

  J_K_Flip_Flop j_k_ff_1 (
    .J(1'b1), .clk(in_3), .K(1'b1), .Q(j_k_ff_1_q), .Qn(out_4[0]), .preset(in_2), .en(xor_1_out));  // open: reset
  J_K_Flip_Flop j_k_ff_2 (
    .J(1'b1), .clk(j_k_ff_1_q), .K(1'b1), .Q(j_k_ff_2_q), .Qn(out_4[1]), .preset(in_2));  // open: en, reset
  J_K_Flip_Flop j_k_ff_3 (
    .J(1'b1), .clk(j_k_ff_2_q), .K(1'b1), .Q(j_k_ff_3_q), .Qn(out_4[2]), .preset(in_2));  // open: en, reset
  J_K_Flip_Flop j_k_ff_4 (.J(1'b1), .clk(j_k_ff_3_q), .K(1'b1), .Qn(out_4[3]), .preset(in_2));  // open: Q, en, reset
  D_Flip_Flop d_ff_1 (.clk(in_3), .D(in_1), .Q(d_ff_1_q), .preset(in_2));  // open: Qn, en, reset
  xor xor_1 (xor_1_out, d_ff_1_q, in_1);
endmodule
