// Logisim project mini project hardware.circ as structural Verilog: 1 circuit, main circuit main
module main (
  input  SET_BOMB,
  input  _00,
  input  _01,
  input  _10,
  input  _11,
  output out_6,
  output out_7,
  output GAME_OVER,
  output _00_2,
  output _01_2,
  output _10_2,
  output _11_2,
  output GAME_WON,
  output COUNTER,
  output out_15
);

  wire and_1_out, and_2_out, and_3_out, and_4_out, and_5_out, and_6_out, and_7_out, and_8_out, and_9_out,
       and_10_out, clock_1_out, d_ff_1_qn, d_ff_3_qn, d_ff_4_qn, d_ff_6_qn, LOCK_IN_out, not_1_out,
       not_2_out, not_3_out, not_4_out, RESET_out;

  Button RESET (.out(RESET_out));
  Clock clock_1 (.out(clock_1_out));
  Button LOCK_IN (.out(LOCK_IN_out));
  not not_1 (not_1_out, SET_BOMB);
  and and_1 (and_1_out, not_1_out, clock_1_out);
  D_Flip_Flop d_ff_1 (
    .clk(and_1_out), .D(d_ff_1_qn), .Q(out_7), .Qn(d_ff_1_qn), .reset(RESET_out));  // open: preset, en
  not not_2 (not_2_out, out_7);
  and and_2 (and_2_out, not_2_out, not_3_out);
  D_Flip_Flop d_ff_2 (.clk(LOCK_IN_out), .D(_00), .Q(_00_2), .reset(RESET_out));  // open: Qn, preset, en
  D_Flip_Flop d_ff_3 (
    .clk(LOCK_IN_out), .D(d_ff_3_qn), .Q(out_15), .Qn(d_ff_3_qn), .reset(RESET_out));  // open: preset, en
  and and_3 (and_3_out, _00_2, and_2_out);
  D_Flip_Flop d_ff_4 (.clk(out_7), .D(d_ff_4_qn), .Q(out_6), .Qn(d_ff_4_qn), .reset(RESET_out));  // open: preset, en
  D_Flip_Flop d_ff_5 (.clk(LOCK_IN_out), .D(_01), .Q(_01_2), .reset(RESET_out));  // open: Qn, preset, en
  not not_3 (not_3_out, out_6);
  and and_4 (and_4_out, out_7, not_3_out);
  D_Flip_Flop d_ff_6 (
    .clk(d_ff_3_qn), .D(d_ff_6_qn), .Q(COUNTER), .Qn(d_ff_6_qn), .reset(RESET_out));  // open: preset, en
  and and_5 (and_5_out, _01_2, and_4_out);
  and and_6 (and_6_out, not_2_out, out_6);
  D_Flip_Flop d_ff_7 (.clk(LOCK_IN_out), .D(_10), .Q(_10_2), .reset(RESET_out));  // open: Qn, preset, en
  and and_7 (and_7_out, _10_2, and_6_out);
  and and_8 (and_8_out, out_7, out_6);
  D_Flip_Flop d_ff_8 (.clk(LOCK_IN_out), .D(_11), .Q(_11_2), .reset(RESET_out));  // open: Qn, preset, en
  and and_9 (and_9_out, _11_2, and_8_out);
  and and_10 (and_10_out, out_15, COUNTER);
  or or_1 (GAME_OVER, and_9_out, and_7_out, and_5_out, and_3_out);
  not not_4 (not_4_out, GAME_OVER);
  and and_11 (GAME_WON, not_4_out, and_10_out);
endmodule
